// Logisim project выставление конфигурации.circ as structural Verilog: 3 circuits, main circuit координаты inc
module \координаты_inc  (
  input  [15:0] String,
  input  btn,
  input  [15:0] Stolb,
  input  \такты ,
  output [15:0] out_5,
  output [15:0] out_6
);

  wire [15:1] and_1_out, and_2_out;
  wire [15:15] and_1_out_2, and_2_out_2;

  assign {and_1_out_2[15], and_1_out} = Stolb & {and_1_out, \такты };  // AND_Gate and_1, 16 bits wide
  Multiplexer multiplexer_1 (.in0(1'b0), .in1(1'b1), .sel(and_1_out_2[15]), .en(and_1_out_2[15]));  // open: out
  assign out_6 = Stolb ^ {and_1_out, \такты };  // XOR_Gate xor_1, 16 bits wide
  assign out_5 = String ^ {and_2_out, btn};  // XOR_Gate xor_2, 16 bits wide
  assign {and_2_out_2[15], and_2_out} = String & {and_2_out, btn};  // AND_Gate and_2, 16 bits wide
  Multiplexer multiplexer_2 (.in0(1'b0), .in1(1'b1), .sel(and_2_out_2[15]), .en(and_2_out_2[15]));  // open: out

  // Other names for the same wires on the sheet: stol = \такты ; str = btn; _0y = Stolb[0]; _1y = Stolb[1];
  //   _2y = Stolb[2]; _3y = Stolb[3]; _4y = Stolb[4]; _5y = Stolb[5]; _6y = Stolb[6]; _7y = Stolb[7]; _8y = Stolb[8];
  //   _9y = Stolb[9]; _10y = Stolb[10]; _11y = Stolb[11]; _12y = Stolb[12]; _13y = Stolb[13]; _14y = Stolb[14];
  //   _15y = Stolb[15]; _0x = String[0]; _2x = String[2]; _3x = String[3]; _4x = String[4]; _5x = String[5];
  //   _6x = String[6]; _7x = String[7]; _8x = String[8]; _9x = String[9]; _10x = String[10]; _11x = String[11];
  //   _12x = String[12]; _13x = String[13]; _14x = String[14]; _15x = String[15]
endmodule

module \координаты_dec  (
  input  [15:0] String,
  input  \такты ,
  input  [15:0] Stolb,
  input  \такты_2 ,
  output [15:0] out_5,
  output [15:0] out_6
);

  wire [15:1] and_1_out, and_2_out;
  wire [15:15] and_1_out_2, and_2_out_2;

  assign {and_1_out_2[15], and_1_out} = {and_1_out, \такты_2 };  // AND_Gate and_1, 16 bits wide AND_Gate
  Multiplexer multiplexer_1 (.in0(1'b0), .in1(1'b1), .sel(and_1_out_2[15]), .en(and_1_out_2[15]));  // open: out
  assign out_6 = ~(Stolb ^ ~{and_1_out, \такты_2 });  // XNOR_Gate xnor_1, 16 bits wide
  assign out_5 = ~(String ^ ~{and_2_out, \такты });  // XNOR_Gate xnor_2, 16 bits wide
  assign {and_2_out_2[15], and_2_out} = {and_2_out, \такты };  // AND_Gate and_2, 16 bits wide AND_Gate
  Multiplexer multiplexer_2 (.in0(1'b0), .in1(1'b1), .sel(and_2_out_2[15]), .en(and_2_out_2[15]));  // open: out

  // Other names for the same wires on the sheet: stol = \такты_2 ; str = \такты ; _0y = Stolb[0]; _1y = Stolb[1];
  //   _2y = Stolb[2]; _3y = Stolb[3]; _4y = Stolb[4]; _5y = Stolb[5]; _6y = Stolb[6]; _7y = Stolb[7]; _8y = Stolb[8];
  //   _9y = Stolb[9]; _10y = Stolb[10]; _11y = Stolb[11]; _12y = Stolb[12]; _13y = Stolb[13]; _14y = Stolb[14];
  //   _15y = Stolb[15]; _0x = String[0]; _2x = String[2]; _3x = String[3]; _4x = String[4]; _5x = String[5];
  //   _6x = String[6]; _7x = String[7]; _8x = String[8]; _9x = String[9]; _10x = String[10]; _11x = String[11];
  //   _12x = String[12]; _13x = String[13]; _14x = String[14]; _15x = String[15]
endmodule

module inc_dec (
  input  btn_start,
  input  btn_plus,
  input  [7:0] start_val,
  input  btn_minus,
  output [7:0] \output 
);

  wire button_1_out, button_3_out, or_1_out, or_2_out, or_3_out;

  Button button_1 (.out(button_1_out));
  Button button_2 ();  // open: out
  or or_1 (or_1_out, btn_plus, btn_minus);
  or or_2 (or_2_out, btn_start, btn_minus);
  Counter #(.max('hf), .ongoal("stay")) counter_1 (
    .load(or_2_out), .D(start_val), .count(or_3_out), .Q(\output ), .clk(or_1_out), .clr(button_3_out));  // open: carry
  or or_3 (or_3_out, btn_plus, btn_plus, btn_minus);
  Button button_3 (.out(button_3_out));
endmodule
