// Logisim project проект2.circ as structural Verilog: 2 circuits, main circuit main
module main (
);

  wire buffer_1_out, buffer_3_out, button_1_out, button_2_out, button_4_out, button_6_out, clock_1_out,
       counter_1_carry, counter_1_q, counter_2_carry, counter_2_q, counter_3_carry, d_ff_1_q, d_ff_1_qn,
       d_ff_2_q, d_ff_2_qn, not_1_out, not_2_out, not_3_out, not_4_out, pull_resistor_5_node,
       pull_resistor_6_node, r2, re1, transistor_13_out, z1, zp1, zp2, \конфиг , \М1 , \М2 , \нач , \старт ;
  wire [3:0] counter_3_q, counter_4_q;
  wire [7:0] transistor_1_out, transistor_2_out, transistor_3_out, x, y, \цдм_1_последнее_считывание_1 ,
       \цдм_1_последнее_считывание_2 , \цдм_1_последнее_считывание_3 ;
  wire [15:0] \память_буфер_1_out_8 , \память_буфер_1_out_9 , \память_буфер_1_out_10 ,
       \память_буфер_1_out_11 , \память_буфер_1_out_12 , \память_буфер_1_out_13 , \память_буфер_1_out_14 ,
       \память_буфер_1_out_15 , \память_буфер_1_out_16 , \память_буфер_1_out_17 , \память_буфер_1_out_18 ,
       \память_буфер_1_out_19 , \память_буфер_1_out_20 , \память_буфер_1_out_21 , \память_буфер_1_out_22 ,
       \память_буфер_1_out_23 , \перевод_из_8_бит_в_16_для_координат_1_out_2 ,
       \перевод_из_8_бит_в_16_для_координат_2_out_2 ;

  Pull_Resistor pull_resistor_1 (.node(\старт ));
  Transistor #(.\type ("n"), .width(8)) transistor_1 (.in(x), .out(transistor_1_out), .gate(\старт ));
  Transistor #(.\type ("n"), .width(8)) transistor_2 (.in(y), .out(transistor_2_out), .gate(\старт ));
  Transistor transistor_3 (.in(re1), .out(transistor_3_out[0]), .gate(\М1 ));
  Transistor transistor_4 (.in(r2), .out(transistor_3_out[0]), .gate(\М2 ));
  not not_1 (not_1_out, \старт );
  \цдм  \u_цдм_1  (
    .\последнее_считывание_1 (\цдм_1_последнее_считывание_1 ),
    .\последнее_считывание_3 (\цдм_1_последнее_считывание_3 ),
    .\последнее_считывание_2 (\цдм_1_последнее_считывание_2 ),
    .\значение_для_записи_2 ({{7{transistor_3_out[7]}}, transistor_3_out[0]}), .on_off(not_1_out));  // open: значение_для_записи_1, значение_для_записи_3
  // Probe on {{7{transistor_3_out[7]}}, transistor_3_out[0]}
  Transistor #(.width(8)) transistor_5 (.in(\цдм_1_последнее_считывание_2 ), .out(transistor_1_out), .gate(\старт ));
  Transistor #(.width(8)) transistor_6 (.in(\цдм_1_последнее_считывание_1 ), .out(transistor_2_out), .gate(\старт ));
  // Probe on transistor_1_out
  // Probe on transistor_2_out
  Pull_Resistor pull_resistor_2 (.node(transistor_3_out[7]));
  Pull_Resistor pull_resistor_3 (.node(zp1));
  Transistor #(.\type ("n")) transistor_7 (.in(transistor_13_out), .out(zp1), .gate(\М1 ));
  Pull_Resistor pull_resistor_4 (.node(zp2));
  Transistor #(.\type ("n")) transistor_8 (.in(transistor_13_out), .out(zp2), .gate(\М2 ));
  // Probe on \цдм_1_последнее_считывание_3 
  Transistor #(.\type ("n"), .gate("br")) transistor_9 (
    .in(pull_resistor_6_node), .out(z1), .gate(\цдм_1_последнее_считывание_3 [2]));
  Transistor #(.\type ("n"), .gate("br")) transistor_10 (
    .in(pull_resistor_6_node), .out(z1), .gate(\цдм_1_последнее_считывание_3 [1]));
  \перевод_из_8_бит_в_16_для_координат  \u_перевод_из_8_бит_в_16_для_координат_1  (
    .in_1(transistor_1_out), .out_2(\перевод_из_8_бит_в_16_для_координат_1_out_2 ));
  \перевод_из_8_бит_в_16_для_координат  \u_перевод_из_8_бит_в_16_для_координат_2  (
    .in_1(transistor_2_out), .out_2(\перевод_из_8_бит_в_16_для_координат_2_out_2 ));
  Transistor #(.\type ("n")) transistor_11 (.in(\конфиг ), .out(zp1), .gate(\старт ));
  not not_2 (not_2_out, re1);
  Transistor #(.\type ("n")) transistor_12 (.in(not_2_out), .out(z1), .gate(\конфиг ));
  Transistor #(.\type ("n")) transistor_13 (
    .in(pull_resistor_5_node), .out(transistor_13_out), .gate(\цдм_1_последнее_считывание_3 [2]));
  Pull_Resistor pull_resistor_5 (.node(pull_resistor_5_node));
  Transistor #(.\type ("n"), .gate("br")) transistor_14 (
    .in(pull_resistor_6_node), .out(transistor_13_out), .gate(\цдм_1_последнее_считывание_3 [1]));
  Pull_Resistor #(.pull(1)) pull_resistor_6 (.node(pull_resistor_6_node));
  \память___буфер  \u_память_буфер_1  (
    .Data(z1), .\запис (zp1), .Return(re1), .String(\перевод_из_8_бит_в_16_для_координат_2_out_2 ),
    .Stolb(\перевод_из_8_бит_в_16_для_координат_1_out_2 ), .out_8(\память_буфер_1_out_8 ),
    .out_9(\память_буфер_1_out_9 ), .out_10(\память_буфер_1_out_10 ), .out_11(\память_буфер_1_out_11 ),
    .out_12(\память_буфер_1_out_12 ), .out_13(\память_буфер_1_out_13 ), .out_14(\память_буфер_1_out_14 ),
    .out_15(\память_буфер_1_out_15 ), .out_16(\память_буфер_1_out_16 ), .out_17(\память_буфер_1_out_17 ),
    .out_18(\память_буфер_1_out_18 ), .out_19(\память_буфер_1_out_19 ), .out_20(\память_буфер_1_out_20 ),
    .out_21(\память_буфер_1_out_21 ), .out_22(\память_буфер_1_out_22 ), .out_23(\память_буфер_1_out_23 ),
    .on_off(\М1 ), .in_4(counter_2_q));
  Pull_Resistor pull_resistor_7 (.node(\М1 ));
  Transistor transistor_15 (.in(d_ff_1_q), .out(\М1 ), .gate(\старт ));
  Pull_Resistor #(.pull(1)) pull_resistor_8 (.node(\М2 ));
  Transistor transistor_16 (.in(not_3_out), .out(\М2 ), .gate(\старт ));
  Counter #(.width(1), .max('h1)) counter_1 (
    .count(d_ff_1_q), .Q(counter_1_q), .carry(counter_1_carry), .clk(\цдм_1_последнее_считывание_3 [0]),
    .clr(counter_1_carry));  // open: load, D
  D_Flip_Flop d_ff_1 (
    .clk(\цдм_1_последнее_считывание_3 [0]), .D(d_ff_1_qn), .Q(d_ff_1_q), .Qn(d_ff_1_qn));  // open: preset, en, reset
  \память___буфер  \u_память_буфер_2  (
    .Data(z1), .\запис (zp2), .Return(r2), .String(\перевод_из_8_бит_в_16_для_координат_2_out_2 ),
    .Stolb(\перевод_из_8_бит_в_16_для_координат_1_out_2 ), .out_8(\память_буфер_1_out_8 ),
    .out_9(\память_буфер_1_out_9 ), .out_10(\память_буфер_1_out_10 ), .out_11(\память_буфер_1_out_11 ),
    .out_12(\память_буфер_1_out_12 ), .out_13(\память_буфер_1_out_13 ), .out_14(\память_буфер_1_out_14 ),
    .out_15(\память_буфер_1_out_15 ), .out_16(\память_буфер_1_out_16 ), .out_17(\память_буфер_1_out_17 ),
    .out_18(\память_буфер_1_out_18 ), .out_19(\память_буфер_1_out_19 ), .out_20(\память_буфер_1_out_20 ),
    .out_21(\память_буфер_1_out_21 ), .out_22(\память_буфер_1_out_22 ), .out_23(\память_буфер_1_out_23 ),
    .on_off(\М2 ), .in_4(counter_1_q));
  Counter #(.width(1), .max('h1)) counter_2 (
    .count(not_3_out), .Q(counter_2_q), .carry(counter_2_carry), .clk(\цдм_1_последнее_считывание_3 [0]),
    .clr(counter_2_carry));  // open: load, D
  not not_3 (not_3_out, d_ff_1_q);
  buf buffer_1 (buffer_1_out, buffer_3_out);
  \Моргает_Красным  \u_моргает_красным_1  (
    .on_off(\старт ), .\Столбец (\перевод_из_8_бит_в_16_для_координат_1_out_2 ), .\такты (clock_1_out),
    .\Строка (\перевод_из_8_бит_в_16_для_координат_2_out_2 ), .out_5(\память_буфер_1_out_8 ),
    .out_6(\память_буфер_1_out_9 ), .out_7(\память_буфер_1_out_10 ), .out_8(\память_буфер_1_out_11 ),
    .out_9(\память_буфер_1_out_12 ), .out_10(\память_буфер_1_out_13 ), .out_11(\память_буфер_1_out_14 ),
    .out_12(\память_буфер_1_out_15 ), .out_13(\память_буфер_1_out_16 ), .out_14(\память_буфер_1_out_17 ),
    .out_15(\память_буфер_1_out_18 ), .out_16(\память_буфер_1_out_19 ), .out_17(\память_буфер_1_out_20 ),
    .out_18(\память_буфер_1_out_21 ), .out_19(\память_буфер_1_out_22 ), .out_20(\память_буфер_1_out_23 ));
  Clock #(.highDuration(1000), .lowDuration(1000)) clock_1 (.out(clock_1_out));
  Counter #(.width(4), .max('ha)) counter_3 (
    .count(\цдм_1_последнее_считывание_3 [0]), .Q(counter_3_q), .carry(counter_3_carry),
    .clk(\цдм_1_последнее_считывание_3 [0]), .clr(buffer_1_out));  // open: load, D
  buf buffer_2 (buffer_1_out, counter_3_carry);
  buf buffer_3 (buffer_3_out, \нач );
  not not_4 (not_4_out, not_4_out);
  DotMatrix #(.inputtype("row"), .matrixcols(16), .matrixrows(16)) dotmatrix_1 (
    .row0(\память_буфер_1_out_8 ), .row1(\память_буфер_1_out_9 ), .row2(\память_буфер_1_out_10 ),
    .row3(\память_буфер_1_out_11 ), .row4(\память_буфер_1_out_12 ), .row5(\память_буфер_1_out_13 ),
    .row6(\память_буфер_1_out_14 ), .row7(\память_буфер_1_out_15 ), .row8(\память_буфер_1_out_16 ),
    .row9(\память_буфер_1_out_17 ), .row10(\память_буфер_1_out_18 ), .row11(\память_буфер_1_out_19 ),
    .row12(\память_буфер_1_out_20 ), .row13(\память_буфер_1_out_21 ), .row14(\память_буфер_1_out_22 ),
    .row15(\память_буфер_1_out_23 ));
  Hex_Digit_Display hex_digit_display_1 (.value(counter_4_q));  // open: dp
  Counter #(.width(4), .max('ha)) counter_4 (
    .count(buffer_1_out), .Q(counter_4_q), .clk(counter_3_carry), .clr(buffer_3_out));  // open: load, D, carry
  Pull_Resistor pull_resistor_9 (.node(buffer_3_out));
  Hex_Digit_Display hex_digit_display_2 (.value(counter_3_q));  // open: dp
  Button button_1 (.out(button_1_out));
  Button button_2 (.out(button_2_out));
  Button button_3 (.out(\конфиг ));
  Button button_4 (.out(button_4_out));
  inc_dec inc_dec_1 (
    .btn_plus(button_2_out), .start_val({8{1'b0}}), .btn_minus(button_6_out), .\output (x));  // open: btn_start
  D_Flip_Flop d_ff_2 (.clk(\нач ), .D(d_ff_2_qn), .Q(d_ff_2_q), .Qn(d_ff_2_qn));  // open: preset, en, reset
  Button button_5 (.out(\нач ));
  Button button_6 (.out(button_6_out));
  inc_dec inc_dec_2 (
    .btn_plus(button_4_out), .start_val({8{1'b0}}), .btn_minus(button_1_out), .\output (y));  // open: btn_start
  not not_5 (\старт , d_ff_2_q);

  // Other names for the same wires on the sheet: z2 = z1

  // Notes on the sheet:
  //   buffer_1 drives only 1 and floats otherwise
  //   buffer_2 drives only 1 and floats otherwise
  //   buffer_3 drives only 1 and floats otherwise
endmodule

module \цдм  (
  input  [7:0] \значение_для_записи_1 ,
  input  [7:0] \значение_для_записи_2 ,
  input  [7:0] \значение_для_записи_3 ,
  input  on_off,
  output [7:0] \последнее_считывание_1 ,
  output [7:0] \последнее_считывание_2 ,
  output [7:0] \последнее_считывание_3 
);

  wire and_1_out, and_2_out, and_3_out, and_4_out, cdm_8_mark5_1_data_inst, cdm_8_mark5_1_mem_cycle, clk,
       clock_1_out, decoder_1_out0, decoder_1_out1, not_1_out, not_2_out, not_3_out, not_4_out, not_5_out,
       or_1_out, r_w, \ср , \ср2 , \ср3 ;
  wire [7:0] cdm_8_mark5_1_data_out, cdm_8_mark5_1_pc, cdm_8_mark5_1_ps, cdm_8_mark5_1_r0, cdm_8_mark5_1_r1,
       cdm_8_mark5_1_r2, cdm_8_mark5_1_r3, cdm_8_mark5_1_sp, controlled_buffer_1_out,
       controlled_buffer_2_out, ram_1_data, \адресс , \работа_с_цдм_1_считалось_с_цдм ,
       \работа_с_цдм_1_шина_записи_2 , \работа_с_цдм_1_шина_чтения_2 , \работа_с_цдм_2_считалось_с_цдм ,
       \работа_с_цдм_2_шина_записи_2 , \работа_с_цдм_2_шина_чтения_2 , \работа_с_цдм_3_считалось_с_цдм ,
       \работа_с_цдм_3_шина_записи_2 , \работа_с_цдм_3_шина_чтения_2 ;

  // Probe on cdm_8_mark5_1_r3
  // Probe on cdm_8_mark5_1_r2
  // Probe on cdm_8_mark5_1_r1
  // Probe on cdm_8_mark5_1_r0
  Pull_Resistor pull_resistor_1 (.node(clk));
  // Probe on cdm_8_mark5_1_sp
  // Probe on cdm_8_mark5_1_pc
  // Probe on cdm_8_mark5_1_ps
  CdM_8_mark5 cdm_8_mark5_1 (
    .clock(clk), .addr(\адресс ), .mem_read(r_w), .mem_cycle(cdm_8_mark5_1_mem_cycle),
    .data_inst(cdm_8_mark5_1_data_inst), .data_out(cdm_8_mark5_1_data_out),
    .data_in(controlled_buffer_2_out), .r0(cdm_8_mark5_1_r0), .r1(cdm_8_mark5_1_r1), .r2(cdm_8_mark5_1_r2),
    .r3(cdm_8_mark5_1_r3), .PC(cdm_8_mark5_1_pc), .SP(cdm_8_mark5_1_sp), .PS(cdm_8_mark5_1_ps));  // open: IAck, IRQ, vec
  Transistor #(.\type ("n")) transistor_1 (.in(clock_1_out), .out(clk), .gate(on_off));
  Clock clock_1 (.out(clock_1_out));
  Decoder #(.disabled(0)) decoder_1 (
    .out0(decoder_1_out0), .out1(decoder_1_out1), .sel(cdm_8_mark5_1_data_inst), .en(cdm_8_mark5_1_mem_cycle));
  not not_1 (not_1_out, r_w);
  assign controlled_buffer_1_out = not_1_out ? cdm_8_mark5_1_data_out : 8'bz;  // Controlled_Buffer controlled_buffer_1
  assign controlled_buffer_2_out = r_w ? \работа_с_цдм_1_шина_записи_2  : 8'bz;  // Controlled_Buffer controlled_buffer_2
  // Probe on \адресс 
  // Probe on controlled_buffer_1_out
  // Probe on \работа_с_цдм_1_шина_записи_2 
  // Probe on 8'hf0
  \работа_с_цдм  \u_работа_с_цдм_1  (
    .\записать_в_цдм (\значение_для_записи_1 ), .\вкл_выкл (decoder_1_out1), .\адресс (\адресс ),
    .\адрес_срабатывания (8'hf0), .\чтение_запись_в_цдм__1_запись (r_w),
    .\считалось_с_цдм (\работа_с_цдм_1_считалось_с_цдм ), .\шина_чтения_2 (\работа_с_цдм_1_шина_чтения_2 ),
    .\шина_записи_2 (\работа_с_цдм_1_шина_записи_2 ), .\сработало (\ср ),
    .\шина_чтения (controlled_buffer_1_out), .\шина_записи (\работа_с_цдм_2_шина_записи_2 ));
  // Probe on \работа_с_цдм_3_шина_чтения_2 
  ROM rom_1 (.addr(\адресс ), .data(\работа_с_цдм_1_шина_записи_2 ), .sel(decoder_1_out0));
  not not_2 (not_2_out, r_w);
  and and_1 (and_1_out, decoder_1_out1, not_5_out);
  not not_3 (not_3_out, clk);
  not not_4 (not_4_out, not_2_out);
  not not_5 (not_5_out, or_1_out);
  or or_1 (or_1_out, \ср , \ср3 , \ср2 );
  Register register_1 (
    .D(\работа_с_цдм_1_считалось_с_цдм ), .Q(\последнее_считывание_1 ), .clk(and_2_out));  // open: en, clr
  and and_2 (and_2_out, \ср , r_w);
  RAM #(.bus("separate")) ram_1 (
    .addr(\адресс ), .din(\работа_с_цдм_3_шина_чтения_2 ), .data(ram_1_data), .str(not_2_out),
    .sel(and_1_out), .clk(not_3_out), .ld(not_4_out));  // open: clr
  // Probe on ram_1_data
  // Probe on \работа_с_цдм_1_шина_чтения_2 
  // Probe on 8'hf1
  \работа_с_цдм  \u_работа_с_цдм_2  (
    .\записать_в_цдм (\значение_для_записи_2 ), .\вкл_выкл (decoder_1_out1), .\адресс (\адресс ),
    .\адрес_срабатывания (8'hf1), .\чтение_запись_в_цдм__1_запись (r_w),
    .\считалось_с_цдм (\работа_с_цдм_2_считалось_с_цдм ), .\шина_чтения_2 (\работа_с_цдм_2_шина_чтения_2 ),
    .\шина_записи_2 (\работа_с_цдм_2_шина_записи_2 ), .\сработало (\ср2 ),
    .\шина_чтения (\работа_с_цдм_1_шина_чтения_2 ), .\шина_записи (\работа_с_цдм_3_шина_записи_2 ));
  Register register_2 (
    .D(\работа_с_цдм_2_считалось_с_цдм ), .Q(\последнее_считывание_2 ), .clk(and_3_out));  // open: en, clr
  and and_3 (and_3_out, \ср2 , r_w);
  // Probe on \работа_с_цдм_2_шина_чтения_2 
  // Probe on 8'hf2
  \работа_с_цдм  \u_работа_с_цдм_3  (
    .\записать_в_цдм (\значение_для_записи_3 ), .\вкл_выкл (decoder_1_out1), .\адресс (\адресс ),
    .\адрес_срабатывания (8'hf2), .\чтение_запись_в_цдм__1_запись (r_w),
    .\считалось_с_цдм (\работа_с_цдм_3_считалось_с_цдм ), .\шина_чтения_2 (\работа_с_цдм_3_шина_чтения_2 ),
    .\шина_записи_2 (\работа_с_цдм_3_шина_записи_2 ), .\сработало (\ср3 ),
    .\шина_чтения (\работа_с_цдм_2_шина_чтения_2 ), .\шина_записи (ram_1_data));
  Register register_3 (
    .D(\работа_с_цдм_3_считалось_с_цдм ), .Q(\последнее_считывание_3 ), .clk(and_4_out));  // open: en, clr
  and and_4 (and_4_out, \ср3 , r_w);

  // Notes on the sheet:
  //   contents of rom_1 (hex, n*v repeats v):
  //   d1 0 d0 f0 a1 d0 e0 a1 d2 0 d0 f1 a2 d0 e1 a2 d0 0 d3 e6 ac d3 f1 bf d0 e5 a3 5 e1 28 d0 f d3 f0 ac
  //   d3 e4 ac ee 32 d3 e0 bc d3 f0 88 ac d3 e4 ac d6 f4 d3 f 77 e1 43 d0 0 d3 f0 ac d3 e2 ac ee 4d d3 e0
  //   bc d3 f0 8c ac d3 e2 ac d6 f4 a e1 59 d0 f d3 f1 ac ee 60 d3 e1 bc 88 d3 f1 ac d6 f4 d3 e0 d6 e8 d6
  //   f4 d3 e4 d6 e8 d6 f4 d3 f 7b e1 7a d0 0 d3 f1 ac ee 81 d3 e1 bc 8c d3 f1 ac d3 e3 ac d6 f4 d3 e2 d6
  //   e8 d6 f4 d3 e0 d6 e8 d6 f4 d0 e1 b0 d3 f1 ac d0 e5 b0 d3 e6 bf 0 e0 bb d0 2 73 e1 ac d0 2 d6 ed ee
  //   b9 d0 3 73 e1 b7 d0 2 d6 ed ee b9 ee c8 ee c8 d0 3 73 e1 c6 d0 2 d6 ed ee c8 ee c8 d0 f 72 e1 dd d0
  //   f 71 e1 d6 ee e2 ee db d3 e2 bd ee 2 ee e2 d3 e3 be ee a d0 1 d6 ed ee 0 bf d0 f0 a3 d7 d3 f2 ac d0
  //   0 ac d7 d3 f1 bc 0 e0 ff d3 e6 bc 8c ac d7
endmodule
